# Fritzing sketch SuongLuongPCB (saved by Fritzing 0.9.3b)
circuit board: 3.49098cm x 5.11415cm
breadboards: 1

parts:
  JP1 = Header 5x2 [package=2x5-raf]
  Part1 = Adafruit TCS34725 RGB Color Sensor [part_number="Adafruit #1334"]

nets:
  N1: JP1.1, Part1.+3V3
  N2: JP1.3, Part1.SDA
  N3: JP1.5, Part1.SCL
  N4: JP1.9, Part1.GND

custom parts:
  Adafruit TCS34725 RGB Color Sensor: Your electronics can now see in dazzling color with this lovely color light sensor. We found the best color sensor on the market, the TCS34725, which has RGB and Clear light sensing elements. An IR blocking filter, integrated on-chip and localized to the color sensing photodiodes, minimizes the IR spectral component of the incoming light and allows color measurements to be made accurately. The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
